// Logisim project 32BITCPU.circ as structural Verilog: 21 circuits, main circuit main
module main (
  output [7:0] out_1
);

  wire andgate_1_out_3, andgate_2_out_3, biggerand_1_out_5, biggerand_2_out_5, biggerand_3_out_5,
       biggerand_4_out_5, biggerand_5_out_5, biggerand_6_out_5, biggerand_7_out_5, biggerand_8_out_5,
       biggerand_9_out_5, biggerand_10_out_5, biggerand_11_out_5, biggerand_12_out_5, biggerand_13_out_5,
       biggerand_14_out_5, biggerand_15_out_5, biggerand_16_out_5, biggerand_17_out_5, biggerand_18_out_5,
       biggerand_19_out_5, biggerand_20_out_5, biggerand_21_out_5, biggerand_22_out_5, biggerand_23_out_5,
       biggerand_24_out_5, biggerand_25_out_5, biggerand_26_out_5, biggerand_27_out_5, biggerand_28_out_5,
       biggerand_29_out_5, biggerand_30_out_5, biggerand_31_out_5, biggerand_32_out_5, biggeror_1_out_13,
       biggeror_2_out_13, biggeror_3_out_13, biggeror_4_out_13, biggeror_5_out_13, biggeror_6_out_13,
       biggeror_7_out_13, biggeror_8_out_13, biggeror_9_out_13, biggeror_10_out_13, biggeror_11_out_13,
       biggeror_12_out_13, biggeror_13_out_13, biggeror_14_out_13, bitswitch_1_out_3, clock_1_out,
       clock_2_out, demux_1_out_5, demux_1_out_6, demux_1_out_7, demux_1_out_8, demux_1_out_9,
       demux_1_out_10, demux_1_out_11, demux_2_out_5, demux_2_out_6, demux_2_out_7, demux_2_out_8,
       demux_2_out_9, demux_2_out_10, demux_2_out_11, demux_2_out_12, demux_3_out_5, demux_3_out_6,
       demux_3_out_7, demux_3_out_8, demux_3_out_9, demux_3_out_10, demux_3_out_11, demux_3_out_12,
       demux_4_out_5, demux_4_out_6, demux_4_out_7, demux_4_out_8, demux_4_out_9, demux_4_out_10,
       demux_5_out_5, demux_5_out_6, demux_5_out_7, demux_5_out_8, demux_5_out_9, demux_5_out_10,
       demux_5_out_11, equal_1_out_3, less_1_out_3, notgate_1_out_2, notgate_2_out_2, notgate_3_out_2,
       notgate_4_out_2, notgate_5_out_2, notgate_6_out_2, notgate_7_out_2, notgate_8_out_2, notgate_9_out_2,
       notgate_10_out_2, notgate_11_out_2, notgate_12_out_2, notgate_13_out_2, notgate_14_out_2,
       notgate_15_out_2, notgate_16_out_2, notgate_17_out_2, orgate_1_out_3, orgate_2_out_3;
  wire [7:0] byteadder_1_outp, byteadder_2_outp, byteneg_1_out_2, bytenot_1_out_2, bytenot_2_out_2,
       bytenot_3_out_2, bytenot_4_out_2, bytenot_5_out_2, bytenot_6_out_2, byteor_1_out_3, byteor_2_out_3,
       byteor_3_out_3, byteor_4_out_3, counter_1_q, counter_2_q, highlevelregister_1_outp,
       highlevelregister_2_outp, highlevelregister_3_outp, highlevelregister_4_outp,
       highlevelregister_5_outp, highlevelregister_6_outp, mux_1_out_4, mux_2_out_4, or_1_out, or_2_out,
       ram_1_dout, ram_2_dout, ram_3_dout, ram_4_dout, stack_1_out_5, switchbuffer_2_outp,
       switchbuffer_3_outp, switchbuffer_4_outp, switchbuffer_5_outp, switchbuffer_6_outp,
       switchbuffer_7_outp, switchbuffer_8_outp, switchbuffer_9_outp, switchbuffer_10_outp,
       switchbuffer_11_outp, switchbuffer_12_outp, switchbuffer_13_outp;

  Counter counter_1 (
    .load(bitswitch_1_out_3), .clk(clock_1_out), .D(ram_4_dout), .Q(counter_1_q));  // open: clr, up, count, carry
  Clock clock_1 (.out(clock_1_out));
  RAM ram_1 (.addr(counter_1_q), .clk(clock_2_out), .dout(ram_1_dout));  // open: we, oe, din
  Clock clock_2 (.out(clock_2_out));
  RAM ram_2 (.addr(counter_1_q), .clk(clock_2_out), .dout(ram_2_dout));  // open: we, oe, din
  RAM ram_3 (.addr(counter_1_q), .clk(clock_2_out), .dout(ram_3_dout));  // open: we, oe, din
  RAM ram_4 (.addr(counter_1_q), .clk(clock_2_out), .dout(ram_4_dout));  // open: we, oe, din
  Counter counter_2 (
    .load(ram_4_dout[6]), .count(ram_4_dout[7]), .clk(clock_2_out), .D(ram_3_dout), .Q(counter_2_q));  // open: clr, up, carry
  stack stack_1 (
    .clock(clock_2_out), .pop(demux_2_out_12), .push(demux_3_out_12), .in_3(ram_4_dout), .out_5(stack_1_out_5));
  notGate notgate_1 (.in_1(ram_4_dout[5]), .out_2(notgate_1_out_2));
  demux demux_1 (
    .in_1(ram_4_dout[2]), .in_2(ram_4_dout[1]), .in_4(ram_4_dout[0]), .in_3(notgate_1_out_2),
    .out_5(demux_1_out_5), .out_6(demux_1_out_6), .out_7(demux_1_out_7), .out_8(demux_1_out_8),
    .out_9(demux_1_out_9), .out_10(demux_1_out_10), .out_11(demux_1_out_11));  // open: out_12
  switchBuffer switchbuffer_1 (.inp(stack_1_out_5), .swt(demux_1_out_11), .outp(out_1));
  switchBuffer switchbuffer_2 (.inp(highlevelregister_1_outp), .swt(demux_2_out_5), .outp(switchbuffer_2_outp));
  HighLevelRegister highlevelregister_1 (
    .save(demux_1_out_5), .inp(stack_1_out_5), .clock(clock_2_out), .outp(highlevelregister_1_outp));
  switchBuffer switchbuffer_3 (.inp(highlevelregister_2_outp), .swt(demux_2_out_6), .outp(switchbuffer_3_outp));
  HighLevelRegister highlevelregister_2 (
    .save(demux_1_out_6), .inp(stack_1_out_5), .clock(clock_2_out), .outp(highlevelregister_2_outp));
  switchBuffer switchbuffer_4 (.inp(highlevelregister_3_outp), .swt(demux_2_out_7), .outp(switchbuffer_4_outp));
  HighLevelRegister highlevelregister_3 (
    .save(demux_1_out_7), .inp(stack_1_out_5), .clock(clock_2_out), .outp(highlevelregister_3_outp));
  switchBuffer switchbuffer_5 (.inp(highlevelregister_4_outp), .swt(demux_2_out_8), .outp(switchbuffer_5_outp));
  HighLevelRegister highlevelregister_4 (
    .save(demux_1_out_8), .inp(stack_1_out_5), .clock(clock_2_out), .outp(highlevelregister_4_outp));
  switchBuffer switchbuffer_6 (.inp(highlevelregister_5_outp), .swt(demux_2_out_9), .outp(switchbuffer_6_outp));
  HighLevelRegister highlevelregister_5 (
    .save(demux_1_out_9), .inp(stack_1_out_5), .clock(clock_2_out), .outp(highlevelregister_5_outp));
  switchBuffer switchbuffer_7 (.inp(highlevelregister_6_outp), .swt(demux_2_out_10), .outp(switchbuffer_7_outp));
  HighLevelRegister highlevelregister_6 (
    .save(demux_1_out_10), .inp(counter_2_q), .clock(clock_2_out), .outp(highlevelregister_6_outp));
  switchBuffer switchbuffer_8 (.inp(highlevelregister_1_outp), .swt(demux_3_out_5), .outp(switchbuffer_8_outp));
  switchBuffer switchbuffer_9 (.inp(highlevelregister_2_outp), .swt(demux_3_out_6), .outp(switchbuffer_9_outp));
  switchBuffer switchbuffer_10 (.inp(highlevelregister_3_outp), .swt(demux_3_out_7), .outp(switchbuffer_10_outp));
  switchBuffer switchbuffer_11 (.inp(highlevelregister_4_outp), .swt(demux_3_out_8), .outp(switchbuffer_11_outp));
  switchBuffer switchbuffer_12 (.inp(highlevelregister_5_outp), .swt(demux_3_out_9), .outp(switchbuffer_12_outp));
  switchBuffer switchbuffer_13 (.inp(highlevelregister_6_outp), .swt(demux_3_out_10), .outp(switchbuffer_13_outp));
  demux demux_2 (
    .in_1(ram_2_dout[2]), .in_2(ram_2_dout[1]), .in_4(ram_2_dout[0]), .in_3(notgate_2_out_2),
    .out_5(demux_2_out_5), .out_6(demux_2_out_6), .out_7(demux_2_out_7), .out_8(demux_2_out_8),
    .out_9(demux_2_out_9), .out_10(demux_2_out_10), .out_11(demux_2_out_11), .out_12(demux_2_out_12));
  notGate notgate_2 (.in_1(ram_2_dout[5]), .out_2(notgate_2_out_2));
  notGate notgate_3 (.in_1(ram_3_dout[5]), .out_2(notgate_3_out_2));
  demux demux_3 (
    .in_1(ram_3_dout[2]), .in_2(ram_3_dout[1]), .in_4(ram_3_dout[0]), .in_3(notgate_3_out_2),
    .out_5(demux_3_out_5), .out_6(demux_3_out_6), .out_7(demux_3_out_7), .out_8(demux_3_out_8),
    .out_9(demux_3_out_9), .out_10(demux_3_out_10), .out_11(demux_3_out_11), .out_12(demux_3_out_12));
  assign or_1_out = switchbuffer_2_outp | switchbuffer_3_outp | switchbuffer_4_outp | switchbuffer_5_outp | switchbuffer_6_outp | switchbuffer_7_outp;  // OR_Gate or_1, 8 bits wide
  assign or_2_out = switchbuffer_8_outp | switchbuffer_9_outp | switchbuffer_10_outp | switchbuffer_11_outp | switchbuffer_12_outp | switchbuffer_13_outp;  // OR_Gate or_2, 8 bits wide
  notGate notgate_4 (.in_1(ram_1_dout[7]), .out_2(notgate_4_out_2));
  notGate notgate_5 (.in_1(ram_1_dout[6]), .out_2(notgate_5_out_2));
  mux mux_1 (.in_1(notgate_5_out_2), .in_2(ram_2_dout), .in_3(or_1_out), .out_4(mux_1_out_4));
  mux mux_2 (.in_1(notgate_4_out_2), .in_2(ram_3_dout), .in_3(or_2_out), .out_4(mux_2_out_4));
  byteAdder byteadder_1 (.b(mux_2_out_4), .a(mux_1_out_4), .outp(byteadder_1_outp));  // open: carry
  byteNeg byteneg_1 (.in_1(mux_2_out_4), .out_2(byteneg_1_out_2));
  byteNot bytenot_1 (.in_1(mux_1_out_4), .out_2(bytenot_1_out_2));
  byteOr byteor_1 (.in_1(bytenot_1_out_2), .in_2(bytenot_2_out_2), .out_3(byteor_1_out_3));
  byteNot bytenot_2 (.in_1(mux_2_out_4), .out_2(bytenot_2_out_2));
  byteOr byteor_2 (.in_1(mux_1_out_4), .in_2(mux_2_out_4), .out_3(byteor_2_out_3));
  byteNot bytenot_3 (.in_1(mux_1_out_4), .out_2(bytenot_3_out_2));
  byteOr byteor_3 (.in_1(bytenot_3_out_2), .in_2(bytenot_4_out_2), .out_3(byteor_3_out_3));
  byteNot bytenot_4 (.in_1(mux_2_out_4), .out_2(bytenot_4_out_2));
  byteOr byteor_4 (.in_1(mux_1_out_4), .in_2(mux_2_out_4), .out_3(byteor_4_out_3));
  RAM ram_5 (
    .addr(highlevelregister_6_outp), .we(demux_3_out_11), .oe(demux_2_out_11), .clk(clock_2_out),
    .din(stack_1_out_5), .dout(stack_1_out_5));
  byteAdder byteadder_2 (.b(byteneg_1_out_2), .a(mux_1_out_4), .outp(byteadder_2_outp));  // open: carry
  byteNot bytenot_5 (.in_1(byteor_1_out_3), .out_2(bytenot_5_out_2));
  byteNot bytenot_6 (.in_1(byteor_2_out_3), .out_2(bytenot_6_out_2));
  switchBuffer switchbuffer_14 (.inp(byteadder_1_outp), .swt(demux_4_out_5), .outp(stack_1_out_5));
  switchBuffer switchbuffer_15 (.inp(byteadder_2_outp), .swt(demux_4_out_6), .outp(stack_1_out_5));
  switchBuffer switchbuffer_16 (.inp(bytenot_5_out_2), .swt(demux_4_out_7), .outp(stack_1_out_5));
  switchBuffer switchbuffer_17 (.inp(bytenot_6_out_2), .swt(demux_4_out_8), .outp(stack_1_out_5));
  switchBuffer switchbuffer_18 (.inp(byteor_3_out_3), .swt(demux_4_out_9), .outp(stack_1_out_5));
  switchBuffer switchbuffer_19 (.inp(byteor_4_out_3), .swt(demux_4_out_10), .outp(stack_1_out_5));
  notGate notgate_6 (.in_1(ram_1_dout[5]), .out_2(notgate_6_out_2));
  demux demux_4 (
    .in_1(ram_1_dout[2]), .in_2(ram_1_dout[1]), .in_4(ram_1_dout[0]), .in_3(notgate_6_out_2),
    .out_5(demux_4_out_5), .out_6(demux_4_out_6), .out_7(demux_4_out_7), .out_8(demux_4_out_8),
    .out_9(demux_4_out_9), .out_10(demux_4_out_10));  // open: out_11, out_12
  equal equal_1 (.in_1(mux_2_out_4), .in_2(mux_1_out_4), .out_3(equal_1_out_3));
  notGate notgate_7 (.in_1(equal_1_out_3), .out_2(notgate_7_out_2));
  less less_1 (.in_1(mux_2_out_4), .in_2(mux_1_out_4), .out_3(less_1_out_3));  // open: out_4
  notGate notgate_8 (.in_1(less_1_out_3), .out_2(notgate_8_out_2));
  notGate notgate_9 (.in_1(equal_1_out_3), .out_2(notgate_9_out_2));
  andGate andgate_1 (.in_1(notgate_7_out_2), .in_2(less_1_out_3), .out_3(andgate_1_out_3));
  orGate orgate_1 (.in_1(equal_1_out_3), .in_2(less_1_out_3), .out_3(orgate_1_out_3));
  andGate andgate_2 (.in_1(notgate_8_out_2), .in_2(notgate_9_out_2), .out_3(andgate_2_out_3));
  orGate orgate_2 (.in_1(notgate_8_out_2), .in_2(equal_1_out_3), .out_3(orgate_2_out_3));
  bitSwitch bitswitch_1 (.in_2(equal_1_out_3), .in_1(demux_5_out_5), .out_3(bitswitch_1_out_3));
  bitSwitch bitswitch_2 (.in_2(notgate_7_out_2), .in_1(demux_5_out_6), .out_3(bitswitch_1_out_3));
  bitSwitch bitswitch_3 (.in_2(andgate_1_out_3), .in_1(demux_5_out_7), .out_3(bitswitch_1_out_3));
  bitSwitch bitswitch_4 (.in_2(orgate_1_out_3), .in_1(demux_5_out_8), .out_3(bitswitch_1_out_3));
  bitSwitch bitswitch_5 (.in_2(andgate_2_out_3), .in_1(demux_5_out_9), .out_3(bitswitch_1_out_3));
  bitSwitch bitswitch_6 (.in_2(orgate_2_out_3), .in_1(demux_5_out_10), .out_3(bitswitch_1_out_3));
  bitSwitch bitswitch_7 (.in_2(1'b1), .in_1(demux_5_out_11), .out_3(bitswitch_1_out_3));
  notGate notgate_10 (.in_1(out_1[4]), .out_2(notgate_10_out_2));
  notGate notgate_11 (.in_1(out_1[5]), .out_2(notgate_11_out_2));
  notGate notgate_12 (.in_1(out_1[6]), .out_2(notgate_12_out_2));
  notGate notgate_13 (.in_1(out_1[7]), .out_2(notgate_13_out_2));
  demux demux_5 (
    .in_1(ram_1_dout[2]), .in_2(ram_1_dout[1]), .in_4(ram_1_dout[0]), .in_3(ram_1_dout[5]),
    .out_5(demux_5_out_5), .out_6(demux_5_out_6), .out_7(demux_5_out_7), .out_8(demux_5_out_8),
    .out_9(demux_5_out_9), .out_10(demux_5_out_10), .out_11(demux_5_out_11));  // open: out_12
  biggerAnd biggerand_1 (
    .in_1(notgate_13_out_2), .in_2(notgate_12_out_2), .in_3(notgate_11_out_2), .in_4(notgate_10_out_2),
    .out_5(biggerand_1_out_5));
  biggerAnd biggerand_2 (
    .in_1(out_1[4]), .in_2(notgate_11_out_2), .in_3(notgate_12_out_2), .in_4(notgate_13_out_2),
    .out_5(biggerand_2_out_5));
  biggerAnd biggerand_3 (
    .in_1(notgate_13_out_2), .in_2(notgate_12_out_2), .in_3(out_1[5]), .in_4(notgate_10_out_2),
    .out_5(biggerand_3_out_5));
  biggerAnd biggerand_4 (
    .in_1(notgate_13_out_2), .in_2(notgate_12_out_2), .in_3(out_1[5]), .in_4(out_1[4]),
    .out_5(biggerand_4_out_5));
  biggerAnd biggerand_5 (
    .in_1(notgate_13_out_2), .in_2(out_1[6]), .in_3(notgate_11_out_2), .in_4(notgate_10_out_2),
    .out_5(biggerand_5_out_5));
  biggerAnd biggerand_6 (
    .in_1(notgate_13_out_2), .in_2(out_1[6]), .in_3(notgate_11_out_2), .in_4(out_1[4]),
    .out_5(biggerand_6_out_5));
  biggerAnd biggerand_7 (
    .in_1(notgate_13_out_2), .in_2(out_1[6]), .in_3(out_1[5]), .in_4(notgate_10_out_2),
    .out_5(biggerand_7_out_5));
  biggerAnd biggerand_8 (
    .in_1(notgate_13_out_2), .in_2(out_1[6]), .in_3(out_1[5]), .in_4(out_1[4]), .out_5(biggerand_8_out_5));
  biggerAnd biggerand_9 (
    .in_1(out_1[7]), .in_2(notgate_12_out_2), .in_3(notgate_11_out_2), .in_4(notgate_10_out_2),
    .out_5(biggerand_9_out_5));
  biggerAnd biggerand_10 (
    .in_1(out_1[7]), .in_2(notgate_12_out_2), .in_3(notgate_11_out_2), .in_4(out_1[4]),
    .out_5(biggerand_10_out_5));
  biggerAnd biggerand_11 (
    .in_1(out_1[7]), .in_2(notgate_12_out_2), .in_3(out_1[5]), .in_4(notgate_10_out_2),
    .out_5(biggerand_11_out_5));
  biggerAnd biggerand_12 (
    .in_1(out_1[7]), .in_2(notgate_12_out_2), .in_3(out_1[5]), .in_4(out_1[4]), .out_5(biggerand_12_out_5));
  biggerAnd biggerand_13 (
    .in_1(out_1[7]), .in_2(out_1[6]), .in_3(notgate_11_out_2), .in_4(notgate_10_out_2),
    .out_5(biggerand_13_out_5));
  biggerAnd biggerand_14 (
    .in_1(out_1[7]), .in_2(out_1[6]), .in_3(notgate_11_out_2), .in_4(out_1[4]), .out_5(biggerand_14_out_5));
  biggerAnd biggerand_15 (
    .in_1(out_1[7]), .in_2(out_1[6]), .in_3(out_1[5]), .in_4(notgate_10_out_2), .out_5(biggerand_15_out_5));
  biggerAnd biggerand_16 (
    .in_1(out_1[7]), .in_2(out_1[6]), .in_3(out_1[5]), .in_4(out_1[4]), .out_5(biggerand_16_out_5));
  biggerOr biggeror_1 (
    .in_1(biggerand_3_out_5), .in_2(biggerand_4_out_5), .in_3(biggerand_5_out_5), .in_4(biggerand_6_out_5),
    .in_5(biggerand_7_out_5), .in_6(biggerand_9_out_5), .in_7(biggerand_10_out_5), .in_8(biggerand_11_out_5),
    .in_9(biggerand_12_out_5), .in_10(biggerand_14_out_5), .in_11(biggerand_15_out_5),
    .in_12(biggerand_16_out_5), .out_13(biggeror_1_out_13));
  biggerOr biggeror_2 (
    .in_1(biggerand_1_out_5), .in_2(biggerand_5_out_5), .in_3(biggerand_6_out_5), .in_4(biggerand_7_out_5),
    .in_5(biggerand_9_out_5), .in_6(biggerand_10_out_5), .in_7(biggerand_11_out_5),
    .in_8(biggerand_13_out_5), .in_9(biggerand_12_out_5), .in_10(biggerand_15_out_5),
    .in_11(biggerand_16_out_5), .out_13(biggeror_2_out_13));  // open: in_12
  biggerOr biggeror_3 (
    .in_1(biggerand_1_out_5), .in_2(biggerand_3_out_5), .in_3(biggerand_4_out_5), .in_4(biggerand_6_out_5),
    .in_5(biggerand_7_out_5), .in_6(biggerand_8_out_5), .in_7(biggerand_9_out_5), .in_8(biggerand_10_out_5),
    .in_9(biggerand_11_out_5), .in_10(biggerand_13_out_5), .in_11(biggerand_15_out_5),
    .in_12(biggerand_16_out_5), .out_13(biggeror_3_out_13));
  biggerOr biggeror_4 (
    .in_1(biggerand_1_out_5), .in_2(biggerand_2_out_5), .in_3(biggerand_3_out_5), .in_4(biggerand_8_out_5),
    .in_5(biggerand_5_out_5), .in_6(biggerand_4_out_5), .in_7(biggerand_9_out_5), .in_8(biggerand_10_out_5),
    .in_9(biggerand_11_out_5), .in_10(biggerand_14_out_5), .out_13(biggeror_4_out_13));  // open: in_11, in_12
  biggerOr biggeror_5 (
    .in_1(biggerand_1_out_5), .in_2(biggerand_3_out_5), .in_3(biggerand_11_out_5), .in_4(biggerand_9_out_5),
    .in_5(biggerand_7_out_5), .in_6(biggerand_12_out_5), .in_7(biggerand_13_out_5),
    .in_8(biggerand_14_out_5), .in_9(biggerand_15_out_5), .in_10(biggerand_16_out_5),
    .out_13(biggeror_5_out_13));  // open: in_11, in_12
  biggerOr biggeror_6 (
    .in_1(biggerand_1_out_5), .in_2(biggerand_12_out_5), .in_3(biggerand_4_out_5), .in_4(biggerand_6_out_5),
    .in_5(biggerand_7_out_5), .in_6(biggerand_9_out_5), .in_7(biggerand_10_out_5), .in_8(biggerand_13_out_5),
    .in_9(biggerand_3_out_5), .in_10(biggerand_14_out_5), .in_11(biggerand_15_out_5),
    .out_13(biggeror_6_out_13));  // open: in_12
  biggerOr biggeror_7 (
    .in_1(biggerand_14_out_5), .in_2(biggerand_2_out_5), .in_3(biggerand_4_out_5), .in_4(biggerand_5_out_5),
    .in_5(biggerand_6_out_5), .in_6(biggerand_7_out_5), .in_7(biggerand_8_out_5), .in_8(biggerand_9_out_5),
    .in_9(biggerand_10_out_5), .in_10(biggerand_11_out_5), .in_11(biggerand_12_out_5),
    .in_12(biggerand_1_out_5), .out_13(biggeror_7_out_13));
  _7_Segment_Display u_7_segment_display_1 (
    .g(biggeror_1_out_13), .f(biggeror_2_out_13), .a(biggeror_3_out_13), .b(biggeror_4_out_13),
    .e(biggeror_5_out_13), .d(biggeror_6_out_13), .c(biggeror_7_out_13));  // open: dp
  notGate notgate_14 (.in_1(out_1[0]), .out_2(notgate_14_out_2));
  notGate notgate_15 (.in_1(out_1[1]), .out_2(notgate_15_out_2));
  _7_Segment_Display u_7_segment_display_2 (
    .g(biggeror_8_out_13), .f(biggeror_9_out_13), .a(biggeror_10_out_13), .b(biggeror_11_out_13),
    .e(biggeror_12_out_13), .d(biggeror_13_out_13), .c(biggeror_14_out_13));  // open: dp
  notGate notgate_16 (.in_1(out_1[2]), .out_2(notgate_16_out_2));
  notGate notgate_17 (.in_1(out_1[3]), .out_2(notgate_17_out_2));
  biggerAnd biggerand_17 (
    .in_1(notgate_17_out_2), .in_2(notgate_16_out_2), .in_3(notgate_15_out_2), .in_4(notgate_14_out_2),
    .out_5(biggerand_17_out_5));
  biggerAnd biggerand_18 (
    .in_1(out_1[0]), .in_2(notgate_15_out_2), .in_3(notgate_16_out_2), .in_4(notgate_17_out_2),
    .out_5(biggerand_18_out_5));
  biggerAnd biggerand_19 (
    .in_1(notgate_17_out_2), .in_2(notgate_16_out_2), .in_3(out_1[1]), .in_4(notgate_14_out_2),
    .out_5(biggerand_19_out_5));
  biggerAnd biggerand_20 (
    .in_1(notgate_17_out_2), .in_2(notgate_16_out_2), .in_3(out_1[1]), .in_4(out_1[0]),
    .out_5(biggerand_20_out_5));
  biggerAnd biggerand_21 (
    .in_1(notgate_17_out_2), .in_2(out_1[2]), .in_3(notgate_15_out_2), .in_4(notgate_14_out_2),
    .out_5(biggerand_21_out_5));
  biggerAnd biggerand_22 (
    .in_1(notgate_17_out_2), .in_2(out_1[2]), .in_3(notgate_15_out_2), .in_4(out_1[0]),
    .out_5(biggerand_22_out_5));
  biggerAnd biggerand_23 (
    .in_1(notgate_17_out_2), .in_2(out_1[2]), .in_3(out_1[1]), .in_4(notgate_14_out_2),
    .out_5(biggerand_23_out_5));
  biggerAnd biggerand_24 (
    .in_1(notgate_17_out_2), .in_2(out_1[2]), .in_3(out_1[1]), .in_4(out_1[0]), .out_5(biggerand_24_out_5));
  biggerAnd biggerand_25 (
    .in_1(out_1[3]), .in_2(notgate_16_out_2), .in_3(notgate_15_out_2), .in_4(notgate_14_out_2),
    .out_5(biggerand_25_out_5));
  biggerAnd biggerand_26 (
    .in_1(out_1[3]), .in_2(notgate_16_out_2), .in_3(notgate_15_out_2), .in_4(out_1[0]),
    .out_5(biggerand_26_out_5));
  biggerAnd biggerand_27 (
    .in_1(out_1[3]), .in_2(notgate_16_out_2), .in_3(out_1[1]), .in_4(notgate_14_out_2),
    .out_5(biggerand_27_out_5));
  biggerAnd biggerand_28 (
    .in_1(out_1[3]), .in_2(notgate_16_out_2), .in_3(out_1[1]), .in_4(out_1[0]), .out_5(biggerand_28_out_5));
  biggerAnd biggerand_29 (
    .in_1(out_1[3]), .in_2(out_1[2]), .in_3(notgate_15_out_2), .in_4(notgate_14_out_2),
    .out_5(biggerand_29_out_5));
  biggerAnd biggerand_30 (
    .in_1(out_1[3]), .in_2(out_1[2]), .in_3(notgate_15_out_2), .in_4(out_1[0]), .out_5(biggerand_30_out_5));
  biggerAnd biggerand_31 (
    .in_1(out_1[3]), .in_2(out_1[2]), .in_3(out_1[1]), .in_4(notgate_14_out_2), .out_5(biggerand_31_out_5));
  biggerAnd biggerand_32 (
    .in_1(out_1[3]), .in_2(out_1[2]), .in_3(out_1[1]), .in_4(out_1[0]), .out_5(biggerand_32_out_5));
  biggerOr biggeror_8 (
    .in_1(biggerand_19_out_5), .in_2(biggerand_20_out_5), .in_3(biggerand_21_out_5),
    .in_4(biggerand_22_out_5), .in_5(biggerand_23_out_5), .in_6(biggerand_25_out_5),
    .in_7(biggerand_26_out_5), .in_8(biggerand_27_out_5), .in_9(biggerand_28_out_5),
    .in_10(biggerand_30_out_5), .in_11(biggerand_31_out_5), .in_12(biggerand_32_out_5),
    .out_13(biggeror_8_out_13));
  biggerOr biggeror_9 (
    .in_1(biggerand_17_out_5), .in_2(biggerand_21_out_5), .in_3(biggerand_22_out_5),
    .in_4(biggerand_23_out_5), .in_5(biggerand_25_out_5), .in_6(biggerand_26_out_5),
    .in_7(biggerand_27_out_5), .in_8(biggerand_29_out_5), .in_9(biggerand_28_out_5),
    .in_10(biggerand_31_out_5), .in_11(biggerand_32_out_5), .out_13(biggeror_9_out_13));  // open: in_12
  biggerOr biggeror_10 (
    .in_1(biggerand_17_out_5), .in_2(biggerand_19_out_5), .in_3(biggerand_20_out_5),
    .in_4(biggerand_22_out_5), .in_5(biggerand_23_out_5), .in_6(biggerand_24_out_5),
    .in_7(biggerand_25_out_5), .in_8(biggerand_26_out_5), .in_9(biggerand_27_out_5),
    .in_10(biggerand_29_out_5), .in_11(biggerand_31_out_5), .in_12(biggerand_32_out_5),
    .out_13(biggeror_10_out_13));
  biggerOr biggeror_11 (
    .in_1(biggerand_17_out_5), .in_2(biggerand_18_out_5), .in_3(biggerand_19_out_5),
    .in_4(biggerand_24_out_5), .in_5(biggerand_21_out_5), .in_6(biggerand_20_out_5),
    .in_7(biggerand_25_out_5), .in_8(biggerand_26_out_5), .in_9(biggerand_27_out_5),
    .in_10(biggerand_30_out_5), .out_13(biggeror_11_out_13));  // open: in_11, in_12
  biggerOr biggeror_12 (
    .in_1(biggerand_17_out_5), .in_2(biggerand_19_out_5), .in_3(biggerand_27_out_5),
    .in_4(biggerand_25_out_5), .in_5(biggerand_23_out_5), .in_6(biggerand_28_out_5),
    .in_7(biggerand_29_out_5), .in_8(biggerand_30_out_5), .in_9(biggerand_31_out_5),
    .in_10(biggerand_32_out_5), .out_13(biggeror_12_out_13));  // open: in_11, in_12
  biggerOr biggeror_13 (
    .in_1(biggerand_17_out_5), .in_2(biggerand_28_out_5), .in_3(biggerand_20_out_5),
    .in_4(biggerand_22_out_5), .in_5(biggerand_23_out_5), .in_6(biggerand_25_out_5),
    .in_7(biggerand_26_out_5), .in_8(biggerand_29_out_5), .in_9(biggerand_19_out_5),
    .in_10(biggerand_30_out_5), .in_11(biggerand_31_out_5), .out_13(biggeror_13_out_13));  // open: in_12
  biggerOr biggeror_14 (
    .in_1(biggerand_30_out_5), .in_2(biggerand_18_out_5), .in_3(biggerand_20_out_5),
    .in_4(biggerand_21_out_5), .in_5(biggerand_22_out_5), .in_6(biggerand_23_out_5),
    .in_7(biggerand_24_out_5), .in_8(biggerand_25_out_5), .in_9(biggerand_26_out_5),
    .in_10(biggerand_27_out_5), .in_11(biggerand_28_out_5), .in_12(biggerand_17_out_5),
    .out_13(biggeror_14_out_13));
endmodule

module fullAdder (
  input  in_1,
  input  in_2,
  input  in_3,
  output carry,
  output sum
);

  wire andgate_1_out_3, andgate_2_out_3, xorgate_1_out_3;

  andGate andgate_1 (.in_1(in_1), .in_2(in_2), .out_3(andgate_1_out_3));
  xorGate xorgate_1 (.in_1(in_1), .in_2(in_2), .out_3(xorgate_1_out_3));
  orGate orgate_1 (.in_1(andgate_1_out_3), .in_2(andgate_2_out_3), .out_3(carry));
  andGate andgate_2 (.in_1(xorgate_1_out_3), .in_2(in_3), .out_3(andgate_2_out_3));
  xorGate xorgate_2 (.in_1(xorgate_1_out_3), .in_2(in_3), .out_3(sum));
endmodule

module byteAdder (
  input  [7:0] a,
  input  [7:0] b,
  output [7:0] outp,
  output carry
);

  wire fulladder_1_carry, fulladder_2_carry, fulladder_3_carry, fulladder_4_carry, fulladder_5_carry,
       fulladder_6_carry, fulladder_7_carry;

  fullAdder fulladder_1 (.in_2(a[0]), .in_3(b[0]), .sum(outp[0]), .carry(fulladder_1_carry));  // open: in_1
  fullAdder fulladder_2 (.in_1(fulladder_1_carry), .in_2(a[1]), .in_3(b[1]), .sum(outp[1]), .carry(fulladder_2_carry));
  fullAdder fulladder_3 (.in_1(fulladder_2_carry), .in_2(a[2]), .in_3(b[2]), .sum(outp[2]), .carry(fulladder_3_carry));
  fullAdder fulladder_4 (.in_1(fulladder_3_carry), .in_2(a[3]), .in_3(b[3]), .sum(outp[3]), .carry(fulladder_4_carry));
  fullAdder fulladder_5 (.in_1(fulladder_4_carry), .in_2(a[4]), .in_3(b[4]), .sum(outp[4]), .carry(fulladder_5_carry));
  fullAdder fulladder_6 (.in_1(fulladder_5_carry), .in_2(a[5]), .in_3(b[5]), .sum(outp[5]), .carry(fulladder_6_carry));
  fullAdder fulladder_7 (.in_1(fulladder_6_carry), .in_2(a[6]), .in_3(b[6]), .sum(outp[6]), .carry(fulladder_7_carry));
  fullAdder fulladder_8 (.in_1(fulladder_7_carry), .in_2(a[7]), .in_3(b[7]), .sum(outp[7]), .carry(carry));
endmodule

module switchBuffer (
  input  swt,
  input  [7:0] inp,
  output [7:0] outp
);

  andGate andgate_1 (.in_1(inp[0]), .in_2(swt), .out_3(outp[0]));
  andGate andgate_2 (.in_1(inp[1]), .in_2(swt), .out_3(outp[1]));
  andGate andgate_3 (.in_1(inp[2]), .in_2(swt), .out_3(outp[2]));
  andGate andgate_4 (.in_1(inp[3]), .in_2(swt), .out_3(outp[3]));
  andGate andgate_5 (.in_1(inp[4]), .in_2(swt), .out_3(outp[4]));
  andGate andgate_6 (.in_1(inp[5]), .in_2(swt), .out_3(outp[5]));
  andGate andgate_7 (.in_1(inp[6]), .in_2(swt), .out_3(outp[6]));
  andGate andgate_8 (.in_1(inp[7]), .in_2(swt), .out_3(outp[7]));
endmodule

module demux (
  input  in_1,
  input  in_2,
  input  in_3,
  input  in_4,
  output out_5,
  output out_6,
  output out_7,
  output out_8,
  output out_9,
  output out_10,
  output out_11,
  output out_12
);

  wire andgate_1_out_3, andgate_2_out_3, andgate_3_out_3, andgate_4_out_3, andgate_5_out_3, andgate_6_out_3,
       andgate_7_out_3, andgate_8_out_3, andgate_9_out_3, andgate_10_out_3, andgate_11_out_3,
       andgate_12_out_3, andgate_13_out_3, andgate_14_out_3, andgate_15_out_3, andgate_16_out_3, not_1_out,
       not_2_out, not_3_out, not_4_out, not_5_out, not_6_out, not_7_out, not_8_out, not_9_out, not_10_out,
       not_11_out, not_12_out;

  not not_1 (not_1_out, in_4);
  not not_2 (not_2_out, in_2);
  not not_3 (not_3_out, in_1);
  not not_4 (not_4_out, in_2);
  not not_5 (not_5_out, in_1);
  not not_6 (not_6_out, in_4);
  not not_7 (not_7_out, in_1);
  not not_8 (not_8_out, in_1);
  not not_9 (not_9_out, in_4);
  not not_10 (not_10_out, in_2);
  not not_11 (not_11_out, in_2);
  not not_12 (not_12_out, in_4);
  andGate andgate_1 (.in_1(not_1_out), .in_2(not_2_out), .out_3(andgate_1_out_3));
  andGate andgate_2 (.in_1(in_4), .in_2(not_4_out), .out_3(andgate_2_out_3));
  andGate andgate_3 (.in_1(not_6_out), .in_2(in_2), .out_3(andgate_3_out_3));
  andGate andgate_4 (.in_1(in_4), .in_2(in_2), .out_3(andgate_4_out_3));
  andGate andgate_5 (.in_1(not_9_out), .in_2(not_10_out), .out_3(andgate_5_out_3));
  andGate andgate_6 (.in_1(in_4), .in_2(not_11_out), .out_3(andgate_6_out_3));
  andGate andgate_7 (.in_1(not_12_out), .in_2(in_2), .out_3(andgate_7_out_3));
  andGate andgate_8 (.in_1(in_4), .in_2(in_2), .out_3(andgate_8_out_3));
  andGate andgate_9 (.in_1(andgate_1_out_3), .in_2(not_3_out), .out_3(andgate_9_out_3));
  andGate andgate_10 (.in_1(andgate_2_out_3), .in_2(not_5_out), .out_3(andgate_10_out_3));
  andGate andgate_11 (.in_1(andgate_3_out_3), .in_2(not_7_out), .out_3(andgate_11_out_3));
  andGate andgate_12 (.in_1(andgate_4_out_3), .in_2(not_8_out), .out_3(andgate_12_out_3));
  andGate andgate_13 (.in_1(andgate_5_out_3), .in_2(in_1), .out_3(andgate_13_out_3));
  andGate andgate_14 (.in_1(andgate_6_out_3), .in_2(in_1), .out_3(andgate_14_out_3));
  andGate andgate_15 (.in_1(andgate_7_out_3), .in_2(in_1), .out_3(andgate_15_out_3));
  andGate andgate_16 (.in_1(andgate_8_out_3), .in_2(in_1), .out_3(andgate_16_out_3));
  andGate andgate_17 (.in_1(in_3), .in_2(andgate_9_out_3), .out_3(out_5));
  andGate andgate_18 (.in_1(in_3), .in_2(andgate_10_out_3), .out_3(out_6));
  andGate andgate_19 (.in_1(in_3), .in_2(andgate_11_out_3), .out_3(out_7));
  andGate andgate_20 (.in_1(in_3), .in_2(andgate_12_out_3), .out_3(out_8));
  andGate andgate_21 (.in_1(in_3), .in_2(andgate_13_out_3), .out_3(out_9));
  andGate andgate_22 (.in_1(in_3), .in_2(andgate_14_out_3), .out_3(out_10));
  andGate andgate_23 (.in_1(in_3), .in_2(andgate_15_out_3), .out_3(out_11));
  andGate andgate_24 (.in_1(in_3), .in_2(andgate_16_out_3), .out_3(out_12));
endmodule

module HighLevelRegister (
  input  clock,
  input  save,
  input  [7:0] inp,
  output [7:0] outp
);

  wire and_1_out;
  wire [7:0] switchbuffer_1_outp;

  switchBuffer switchbuffer_1 (.inp(inp), .swt(save), .outp(switchbuffer_1_outp));
  and and_1 (and_1_out, save, clock);
  D_Flip_Flop #(.trigger("high")) d_ff_1 (
    .D(switchbuffer_1_outp[0]), .clk(and_1_out), .Q(outp[0]));  // open: Qn, preset, reset
  D_Flip_Flop #(.trigger("high")) d_ff_2 (
    .D(switchbuffer_1_outp[1]), .clk(and_1_out), .Q(outp[1]));  // open: Qn, preset, reset
  D_Flip_Flop #(.trigger("high")) d_ff_3 (
    .D(switchbuffer_1_outp[2]), .clk(and_1_out), .Q(outp[2]));  // open: Qn, preset, reset
  D_Flip_Flop #(.trigger("high")) d_ff_4 (
    .D(switchbuffer_1_outp[3]), .clk(and_1_out), .Q(outp[3]));  // open: Qn, preset, reset
  D_Flip_Flop #(.trigger("high")) d_ff_5 (
    .D(switchbuffer_1_outp[4]), .clk(and_1_out), .Q(outp[4]));  // open: Qn, preset, reset
  D_Flip_Flop #(.trigger("high")) d_ff_6 (
    .D(switchbuffer_1_outp[5]), .clk(and_1_out), .Q(outp[5]));  // open: Qn, preset, reset
  D_Flip_Flop #(.trigger("high")) d_ff_7 (
    .D(switchbuffer_1_outp[6]), .clk(and_1_out), .Q(outp[6]));  // open: Qn, preset, reset
  D_Flip_Flop #(.trigger("high")) d_ff_8 (
    .D(switchbuffer_1_outp[7]), .clk(and_1_out), .Q(outp[7]));  // open: Qn, preset, reset
endmodule

module mux (
  input  in_1,
  input  [7:0] in_2,
  input  [7:0] in_3,
  output [7:0] out_4
);

  wire notgate_1_out_2;
  wire [7:0] switchbuffer_1_outp, switchbuffer_2_outp;

  notGate notgate_1 (.in_1(in_1), .out_2(notgate_1_out_2));
  switchBuffer switchbuffer_1 (.inp(in_2), .swt(notgate_1_out_2), .outp(switchbuffer_1_outp));
  switchBuffer switchbuffer_2 (.inp(in_3), .swt(in_1), .outp(switchbuffer_2_outp));
  byteAdder byteadder_1 (.b(switchbuffer_2_outp), .a(switchbuffer_1_outp), .outp(out_4));  // open: carry
endmodule

module notGate (
  input  in_1,
  output out_2
);

  nand nand_1 (out_2, in_1, in_1);
endmodule

module andGate (
  input  in_1,
  input  in_2,
  output out_3
);

  wire nand_1_out;

  nand nand_1 (nand_1_out, in_1, in_2);
  notGate notgate_1 (.in_1(nand_1_out), .out_2(out_3));
endmodule

module orGate (
  input  in_1,
  input  in_2,
  output out_3
);

  wire notgate_1_out_2, notgate_2_out_2;

  notGate notgate_1 (.in_1(in_1), .out_2(notgate_1_out_2));
  notGate notgate_2 (.in_1(in_2), .out_2(notgate_2_out_2));
  nand nand_1 (out_3, notgate_1_out_2, notgate_2_out_2);
endmodule

module norGate (
  input  in_1,
  input  in_2,
  output out_3
);

  wire nand_1_out, notgate_1_out_2, notgate_2_out_2;

  notGate notgate_1 (.in_1(in_1), .out_2(notgate_1_out_2));
  nand nand_1 (nand_1_out, notgate_1_out_2, notgate_2_out_2);
  notGate notgate_2 (.in_1(in_2), .out_2(notgate_2_out_2));
  notGate notgate_3 (.in_1(nand_1_out), .out_2(out_3));
endmodule

module xorGate (
  input  in_1,
  input  in_2,
  output out_3
);

  wire nand_1_out, orgate_1_out_3;

  nand nand_1 (nand_1_out, in_1, in_2);
  orGate orgate_1 (.in_1(in_1), .in_2(in_2), .out_3(orgate_1_out_3));
  andGate andgate_1 (.in_1(nand_1_out), .in_2(orgate_1_out_3), .out_3(out_3));
endmodule

module byteNeg (
  input  [7:0] in_1,
  output [7:0] out_2
);

  wire fulladder_1_carry, fulladder_2_carry, fulladder_3_carry, fulladder_4_carry, fulladder_5_carry,
       fulladder_6_carry, fulladder_7_carry;
  wire [7:0] bytenot_1_out_2;

  fullAdder fulladder_1 (
    .in_1(1'b1), .in_3(bytenot_1_out_2[0]), .sum(out_2[7]), .carry(fulladder_1_carry));  // open: in_2
  byteNot bytenot_1 (.in_1(in_1), .out_2(bytenot_1_out_2));
  fullAdder fulladder_2 (
    .in_1(fulladder_1_carry), .in_3(bytenot_1_out_2[1]), .sum(out_2[6]), .carry(fulladder_2_carry));  // open: in_2
  fullAdder fulladder_3 (
    .in_1(fulladder_2_carry), .in_3(bytenot_1_out_2[2]), .sum(out_2[5]), .carry(fulladder_3_carry));  // open: in_2
  fullAdder fulladder_4 (
    .in_1(fulladder_3_carry), .in_3(bytenot_1_out_2[3]), .sum(out_2[4]), .carry(fulladder_4_carry));  // open: in_2
  fullAdder fulladder_5 (
    .in_1(fulladder_4_carry), .in_3(bytenot_1_out_2[4]), .sum(out_2[3]), .carry(fulladder_5_carry));  // open: in_2
  fullAdder fulladder_6 (
    .in_1(fulladder_5_carry), .in_3(bytenot_1_out_2[5]), .sum(out_2[2]), .carry(fulladder_6_carry));  // open: in_2
  fullAdder fulladder_7 (
    .in_1(fulladder_6_carry), .in_3(bytenot_1_out_2[6]), .sum(out_2[1]), .carry(fulladder_7_carry));  // open: in_2
  fullAdder fulladder_8 (.in_1(fulladder_7_carry), .in_3(bytenot_1_out_2[7]), .sum(out_2[0]));  // open: in_2, carry
endmodule

module byteNot (
  input  [7:0] in_1,
  output [7:0] out_2
);

  notGate notgate_1 (.in_1(in_1[0]), .out_2(out_2[0]));
  notGate notgate_2 (.in_1(in_1[1]), .out_2(out_2[1]));
  notGate notgate_3 (.in_1(in_1[2]), .out_2(out_2[2]));
  notGate notgate_4 (.in_1(in_1[3]), .out_2(out_2[3]));
  notGate notgate_5 (.in_1(in_1[4]), .out_2(out_2[4]));
  notGate notgate_6 (.in_1(in_1[5]), .out_2(out_2[5]));
  notGate notgate_7 (.in_1(in_1[6]), .out_2(out_2[6]));
  notGate notgate_8 (.in_1(in_1[7]), .out_2(out_2[7]));
endmodule

module byteOr (
  input  [7:0] in_1,
  input  [7:0] in_2,
  output [7:0] out_3
);

  orGate orgate_1 (.in_1(in_1[0]), .in_2(in_2[0]), .out_3(out_3[0]));
  orGate orgate_2 (.in_1(in_1[1]), .in_2(in_2[1]), .out_3(out_3[1]));
  orGate orgate_3 (.in_1(in_1[2]), .in_2(in_2[2]), .out_3(out_3[2]));
  orGate orgate_4 (.in_1(in_1[3]), .in_2(in_2[3]), .out_3(out_3[3]));
  orGate orgate_5 (.in_1(in_1[4]), .in_2(in_2[4]), .out_3(out_3[4]));
  orGate orgate_6 (.in_1(in_1[5]), .in_2(in_2[5]), .out_3(out_3[5]));
  orGate orgate_7 (.in_1(in_1[6]), .in_2(in_2[6]), .out_3(out_3[6]));
  orGate orgate_8 (.in_1(in_1[7]), .in_2(in_2[7]), .out_3(out_3[7]));
endmodule

module equal (
  input  [7:0] in_1,
  input  [7:0] in_2,
  output out_3
);

  wire andgate_1_out_3, andgate_2_out_3, andgate_3_out_3, andgate_4_out_3, andgate_5_out_3, andgate_6_out_3,
       notgate_1_out_2, notgate_2_out_2, notgate_3_out_2, notgate_4_out_2, notgate_5_out_2, notgate_6_out_2,
       notgate_7_out_2, notgate_8_out_2, xorgate_1_out_3, xorgate_2_out_3, xorgate_3_out_3, xorgate_4_out_3,
       xorgate_5_out_3, xorgate_6_out_3, xorgate_7_out_3, xorgate_8_out_3;

  xorGate xorgate_1 (.in_1(in_1[0]), .in_2(in_2[0]), .out_3(xorgate_1_out_3));
  notGate notgate_1 (.in_1(xorgate_1_out_3), .out_2(notgate_1_out_2));
  xorGate xorgate_2 (.in_1(in_1[1]), .in_2(in_2[1]), .out_3(xorgate_2_out_3));
  notGate notgate_2 (.in_1(xorgate_2_out_3), .out_2(notgate_2_out_2));
  xorGate xorgate_3 (.in_1(in_1[2]), .in_2(in_2[2]), .out_3(xorgate_3_out_3));
  notGate notgate_3 (.in_1(xorgate_3_out_3), .out_2(notgate_3_out_2));
  xorGate xorgate_4 (.in_1(in_1[3]), .in_2(in_2[3]), .out_3(xorgate_4_out_3));
  notGate notgate_4 (.in_1(xorgate_4_out_3), .out_2(notgate_4_out_2));
  xorGate xorgate_5 (.in_1(in_1[4]), .in_2(in_2[4]), .out_3(xorgate_5_out_3));
  notGate notgate_5 (.in_1(xorgate_5_out_3), .out_2(notgate_5_out_2));
  xorGate xorgate_6 (.in_1(in_1[5]), .in_2(in_2[5]), .out_3(xorgate_6_out_3));
  notGate notgate_6 (.in_1(xorgate_6_out_3), .out_2(notgate_6_out_2));
  xorGate xorgate_7 (.in_1(in_1[6]), .in_2(in_2[6]), .out_3(xorgate_7_out_3));
  notGate notgate_7 (.in_1(xorgate_7_out_3), .out_2(notgate_7_out_2));
  xorGate xorgate_8 (.in_1(in_1[7]), .in_2(in_2[7]), .out_3(xorgate_8_out_3));
  notGate notgate_8 (.in_1(xorgate_8_out_3), .out_2(notgate_8_out_2));
  andGate andgate_1 (.in_1(notgate_1_out_2), .in_2(notgate_2_out_2), .out_3(andgate_1_out_3));
  andGate andgate_2 (.in_1(andgate_1_out_3), .in_2(andgate_3_out_3), .out_3(andgate_2_out_3));
  andGate andgate_3 (.in_1(notgate_3_out_2), .in_2(notgate_4_out_2), .out_3(andgate_3_out_3));
  andGate andgate_4 (.in_1(notgate_5_out_2), .in_2(notgate_6_out_2), .out_3(andgate_4_out_3));
  andGate andgate_5 (.in_1(andgate_4_out_3), .in_2(andgate_6_out_3), .out_3(andgate_5_out_3));
  andGate andgate_6 (.in_1(notgate_7_out_2), .in_2(notgate_8_out_2), .out_3(andgate_6_out_3));
  andGate andgate_7 (.in_1(andgate_2_out_3), .in_2(andgate_5_out_3), .out_3(out_3));
endmodule

module less (
  input  [7:0] in_1,
  input  [7:0] in_2,
  output out_3,
  output out_4
);

  wire andgate_1_out_3, andgate_2_out_3, demux_1_out_5, demux_1_out_6, demux_1_out_7, demux_1_out_8,
       orgate_1_out_3, orgate_2_out_3;
  wire [7:0] byteadder_1_outp, byteneg_1_out_2;

  byteNeg byteneg_1 (.in_1(in_2), .out_2(byteneg_1_out_2));
  byteAdder byteadder_1 (.b(byteneg_1_out_2), .a(in_1), .outp(byteadder_1_outp));  // open: carry
  demux demux_1 (
    .in_2(in_2[7]), .in_4(in_1[7]), .in_3(1'b1), .out_5(demux_1_out_5), .out_6(demux_1_out_6),
    .out_7(demux_1_out_7), .out_8(demux_1_out_8));  // open: in_1, out_9, out_10, out_11, out_12
  orGate orgate_1 (.in_1(demux_1_out_5), .in_2(demux_1_out_8), .out_3(orgate_1_out_3));
  orGate orgate_2 (.in_1(demux_1_out_5), .in_2(demux_1_out_6), .out_3(orgate_2_out_3));
  andGate andgate_1 (.in_1(orgate_1_out_3), .in_2(byteadder_1_outp[7]), .out_3(andgate_1_out_3));
  andGate andgate_2 (.in_1(orgate_2_out_3), .in_2(byteadder_1_outp[7]), .out_3(andgate_2_out_3));
  orGate orgate_3 (.in_1(andgate_2_out_3), .in_2(demux_1_out_6), .out_3(out_4));
  orGate orgate_4 (.in_1(andgate_1_out_3), .in_2(demux_1_out_7), .out_3(out_3));
endmodule

module bitSwitch (
  input  in_1,
  input  in_2,
  output out_3
);

  andGate andgate_1 (.in_1(in_1), .in_2(in_2), .out_3(out_3));
endmodule

module stack (
  input  pop,
  input  push,
  input  [7:0] in_3,
  input  clock,
  output [7:0] out_5
);

  wire andgate_1_out_3, orgate_1_out_3;
  wire [7:0] counter_1_q, ram_1_dout;

  orGate orgate_1 (.in_1(pop), .in_2(push), .out_3(orgate_1_out_3));
  RAM #(.trigger("high")) ram_1 (.addr(counter_1_q), .we(push), .oe(pop), .din(in_3), .dout(ram_1_dout));
  Counter counter_1 (.up(push), .count(orgate_1_out_3), .clk(clock), .Q(counter_1_q));  // open: clr, load, D, carry
  andGate andgate_1 (.in_1(pop), .in_2(clock), .out_3(andgate_1_out_3));
  switchBuffer switchbuffer_1 (.inp(ram_1_dout), .swt(andgate_1_out_3), .outp(out_5));
endmodule

module biggerAnd (
  input  in_1,
  input  in_2,
  input  in_3,
  input  in_4,
  output out_5
);

  wire andgate_1_out_3, andgate_2_out_3;

  andGate andgate_1 (.in_1(in_1), .in_2(in_2), .out_3(andgate_1_out_3));
  andGate andgate_2 (.in_1(in_3), .in_2(in_4), .out_3(andgate_2_out_3));
  andGate andgate_3 (.in_1(andgate_1_out_3), .in_2(andgate_2_out_3), .out_3(out_5));
endmodule

module biggerOr (
  input  in_1,
  input  in_2,
  input  in_3,
  input  in_4,
  input  in_5,
  input  in_6,
  input  in_7,
  input  in_8,
  input  in_9,
  input  in_10,
  input  in_11,
  input  in_12,
  output out_13
);

  wire orgate_1_out_3, orgate_2_out_3, orgate_3_out_3, orgate_4_out_3, orgate_5_out_3, orgate_6_out_3,
       orgate_7_out_3, orgate_8_out_3, orgate_9_out_3, orgate_10_out_3;

  orGate orgate_1 (.in_1(in_1), .in_2(in_2), .out_3(orgate_1_out_3));
  orGate orgate_2 (.in_1(orgate_1_out_3), .in_2(orgate_3_out_3), .out_3(orgate_2_out_3));
  orGate orgate_3 (.in_1(in_3), .in_2(in_4), .out_3(orgate_3_out_3));
  orGate orgate_4 (.in_1(in_5), .in_2(in_6), .out_3(orgate_4_out_3));
  orGate orgate_5 (.in_1(orgate_4_out_3), .in_2(orgate_6_out_3), .out_3(orgate_5_out_3));
  orGate orgate_6 (.in_1(in_7), .in_2(in_8), .out_3(orgate_6_out_3));
  orGate orgate_7 (.in_1(in_9), .in_2(in_10), .out_3(orgate_7_out_3));
  orGate orgate_8 (.in_1(orgate_7_out_3), .in_2(orgate_9_out_3), .out_3(orgate_8_out_3));
  orGate orgate_9 (.in_1(in_11), .in_2(in_12), .out_3(orgate_9_out_3));
  orGate orgate_10 (.in_1(orgate_2_out_3), .in_2(orgate_5_out_3), .out_3(orgate_10_out_3));
  orGate orgate_11 (.in_1(orgate_10_out_3), .in_2(orgate_8_out_3), .out_3(out_13));
endmodule
