// Logisim project CPU.circ as structural Verilog: 1 circuit, main circuit main
module main (
  input  Dec,
  input  [7:0] in_2,
  output [7:0] Outp
);

  wire and_2_out, and_3_out, and_4_out, and_5_out, and_6_out, and_7_out, and_8_out, and_9_out, and_10_out,
       and_11_out, and_12_out, and_13_out, and_14_out, and_15_out, and_16_out, and_17_out, and_18_out,
       and_19_out, and_20_out, and_21_out, and_22_out, and_23_out, and_24_out, and_25_out, and_26_out,
       and_27_out, and_28_out, and_29_out, and_30_out, and_31_out, and_32_out, and_33_out, and_34_out,
       clock_1_out, clock_2_out, clock_3_out, controlled_buffer_14_out, decoder_1_out0, decoder_1_out1,
       decoder_1_out2, decoder_1_out3, decoder_2_out0, decoder_2_out1, decoder_2_out2, decoder_2_out3,
       decoder_2_out4, decoder_2_out5, decoder_2_out6, decoder_3_out0, decoder_3_out1, decoder_3_out2,
       decoder_3_out3, decoder_3_out4, decoder_3_out5, decoder_3_out6, decoder_4_out0, decoder_4_out1,
       decoder_4_out2, decoder_4_out3, decoder_4_out4, decoder_4_out5, decoder_5_out1, decoder_5_out2,
       decoder_5_out3, decoder_5_out4, decoder_5_out5, decoder_5_out6, decoder_5_out7, nor_2_out, not_1_out,
       not_2_out, not_3_out, not_4_out, not_5_out, not_6_out, not_7_out, not_8_out, not_9_out, not_10_out,
       not_11_out, not_12_out, or_1_out, or_3_out, or_4_out, or_5_out, or_6_out, or_7_out, or_8_out,
       or_9_out, or_10_out, or_11_out, or_12_out, or_13_out, or_14_out, or_15_out, or_16_out, or_17_out,
       or_18_out, or_19_out;
  wire [1:0] InstructionMemory_dout;
  wire [2:0] InstructionMemory_dout_2, InstructionMemory_dout_3;
  wire [7:0] adder_1_out, and_1_out, controlled_buffer_1_out, controlled_buffer_7_out, InstructionCounter_q,
       nand_1_out, nor_1_out, or_2_out, Reg_0_q, Reg_1_q, Reg_2_q, Reg_3_q, Reg_4_q, Reg_5_q, Reg_Temp_q,
       subtractor_1_out;

  Clock clock_1 (.out(clock_1_out));
  Counter InstructionCounter (
    .load(controlled_buffer_14_out), .clk(clock_1_out), .D(Reg_0_q), .Q(InstructionCounter_q));  // open: clr, up, count, carry
  Clock clock_2 (.out(clock_2_out));
  RAM #(.trigger("falling")) InstructionMemory (
    .addr(InstructionCounter_q), .clk(clock_2_out),
    .dout({InstructionMemory_dout, InstructionMemory_dout_2, InstructionMemory_dout_3}));  // open: we, oe, din
  Decoder #(.select(2)) decoder_1 (
    .out0(decoder_1_out0), .out1(decoder_1_out1), .out2(decoder_1_out2), .out3(decoder_1_out3),
    .sel(InstructionMemory_dout), .en(Dec));
  Decoder #(.select(3)) decoder_2 (
    .out0(decoder_2_out0), .out1(decoder_2_out1), .out2(decoder_2_out2), .out3(decoder_2_out3),
    .out4(decoder_2_out4), .out5(decoder_2_out5), .out6(decoder_2_out6), .sel(InstructionMemory_dout_3),
    .en(decoder_1_out1));  // open: out7
  Register #(.trigger("high")) Reg_out (
    .D(controlled_buffer_1_out), .en(clock_3_out), .clk(decoder_2_out6), .Q(Outp));  // open: clr
  Register #(.trigger("high")) Reg_0 (
    .D({InstructionMemory_dout, InstructionMemory_dout_2, InstructionMemory_dout_3}), .en(clock_3_out),
    .clk(decoder_1_out0), .Q(Reg_0_q));  // open: clr
  Register #(.trigger("high")) Reg_1 (
    .D(controlled_buffer_7_out), .en(clock_3_out), .clk(decoder_2_out0), .Q(Reg_1_q));  // open: clr
  Register #(.trigger("high")) Reg_2 (
    .D(controlled_buffer_7_out), .en(clock_3_out), .clk(decoder_2_out1), .Q(Reg_2_q));  // open: clr
  Register #(.trigger("high")) Reg_3 (
    .D(controlled_buffer_7_out), .en(clock_3_out), .clk(or_1_out), .Q(Reg_3_q));  // open: clr
  or or_1 (or_1_out, decoder_2_out2, decoder_1_out2);
  Register #(.trigger("high")) Reg_4 (
    .D(controlled_buffer_7_out), .en(clock_3_out), .clk(decoder_2_out3), .Q(Reg_4_q));  // open: clr
  Register #(.trigger("high")) Reg_5 (
    .D(controlled_buffer_7_out), .en(clock_3_out), .clk(decoder_2_out4), .Q(Reg_5_q));  // open: clr
  Clock clock_3 (.out(clock_3_out));
  assign controlled_buffer_1_out = decoder_3_out0 ? Reg_0_q : 8'bz;  // Controlled_Buffer controlled_buffer_1
  assign controlled_buffer_1_out = decoder_3_out1 ? Reg_1_q : 8'bz;  // Controlled_Buffer controlled_buffer_2
  assign controlled_buffer_1_out = decoder_3_out2 ? Reg_2_q : 8'bz;  // Controlled_Buffer controlled_buffer_3
  assign controlled_buffer_1_out = decoder_3_out3 ? Reg_3_q : 8'bz;  // Controlled_Buffer controlled_buffer_4
  assign controlled_buffer_1_out = decoder_3_out4 ? Reg_4_q : 8'bz;  // Controlled_Buffer controlled_buffer_5
  assign controlled_buffer_1_out = decoder_3_out5 ? Reg_5_q : 8'bz;  // Controlled_Buffer controlled_buffer_6
  Decoder #(.select(3)) decoder_3 (
    .out0(decoder_3_out0), .out1(decoder_3_out1), .out2(decoder_3_out2), .out3(decoder_3_out3),
    .out4(decoder_3_out4), .out5(decoder_3_out5), .out6(decoder_3_out6), .sel(InstructionMemory_dout_2),
    .en(decoder_1_out1));  // open: out7
  assign controlled_buffer_7_out = decoder_3_out6 ? Reg_Temp_q : 8'bz;  // Controlled_Buffer controlled_buffer_7
  Decoder #(.select(3)) decoder_4 (
    .out0(decoder_4_out0), .out1(decoder_4_out1), .out2(decoder_4_out2), .out3(decoder_4_out3),
    .out4(decoder_4_out4), .out5(decoder_4_out5), .sel(InstructionMemory_dout_3), .en(decoder_1_out2));  // open: out6, out7
  Register #(.trigger("high")) Reg_Temp (
    .D(controlled_buffer_1_out), .en(clock_3_out), .clk(decoder_2_out5), .Q(Reg_Temp_q));  // open: clr
  assign or_2_out = Reg_1_q | Reg_2_q;  // OR_Gate or_2, 8 bits wide
  assign nand_1_out = ~(Reg_1_q & Reg_2_q);  // NAND_Gate nand_1, 8 bits wide
  assign nor_1_out = ~(Reg_1_q | Reg_2_q);  // NOR_Gate nor_1, 8 bits wide
  assign and_1_out = Reg_1_q & Reg_2_q;  // AND_Gate and_1, 8 bits wide
  Adder adder_1 (.a(Reg_1_q), .b(Reg_2_q), .out(adder_1_out));  // open: cin, cout
  Subtractor subtractor_1 (.a(Reg_1_q), .b(Reg_2_q), .out(subtractor_1_out));  // open: bin, bout
  assign controlled_buffer_7_out = decoder_4_out0 ? or_2_out : 8'bz;  // Controlled_Buffer controlled_buffer_8
  assign controlled_buffer_7_out = decoder_4_out1 ? nand_1_out : 8'bz;  // Controlled_Buffer controlled_buffer_9
  assign controlled_buffer_7_out = decoder_4_out2 ? nor_1_out : 8'bz;  // Controlled_Buffer controlled_buffer_10
  assign controlled_buffer_7_out = decoder_4_out3 ? and_1_out : 8'bz;  // Controlled_Buffer controlled_buffer_11
  assign controlled_buffer_7_out = decoder_4_out4 ? adder_1_out : 8'bz;  // Controlled_Buffer controlled_buffer_12
  assign controlled_buffer_7_out = decoder_4_out5 ? subtractor_1_out : 8'bz;  // Controlled_Buffer controlled_buffer_13
  nor nor_2 (nor_2_out, Reg_3_q[0], Reg_3_q[1], Reg_3_q[2], Reg_3_q[3], Reg_3_q[4], Reg_3_q[5], Reg_3_q[6], Reg_3_q[7]);
  buf or_3 (or_3_out, Reg_3_q[7]);  // OR_Gate
  not not_1 (not_1_out, nor_2_out);
  not not_2 (not_2_out, Reg_3_q[7]);
  or or_4 (or_4_out, nor_2_out, or_3_out);
  not not_3 (not_3_out, nor_2_out);
  or or_5 (or_5_out, nor_2_out, not_4_out);
  not not_4 (not_4_out, Reg_3_q[7]);
  and and_2 (and_2_out, not_1_out, not_2_out);
  Decoder #(.select(3)) decoder_5 (
    .out1(decoder_5_out1), .out2(decoder_5_out2), .out3(decoder_5_out3), .out4(decoder_5_out4),
    .out5(decoder_5_out5), .out6(decoder_5_out6), .out7(decoder_5_out7), .sel(InstructionMemory_dout_3),
    .en(decoder_1_out3));  // open: out0
  assign controlled_buffer_14_out = decoder_5_out1 ? nor_2_out : 1'bz;  // Controlled_Buffer controlled_buffer_14
  assign controlled_buffer_14_out = decoder_5_out2 ? or_3_out : 1'bz;  // Controlled_Buffer controlled_buffer_15
  assign controlled_buffer_14_out = decoder_5_out3 ? or_4_out : 1'bz;  // Controlled_Buffer controlled_buffer_16
  assign controlled_buffer_14_out = decoder_5_out4 ? 1'b1 : 1'bz;  // Controlled_Buffer controlled_buffer_17
  assign controlled_buffer_14_out = decoder_5_out5 ? not_3_out : 1'bz;  // Controlled_Buffer controlled_buffer_18
  assign controlled_buffer_14_out = decoder_5_out6 ? or_5_out : 1'bz;  // Controlled_Buffer controlled_buffer_19
  assign controlled_buffer_14_out = decoder_5_out7 ? and_2_out : 1'bz;  // Controlled_Buffer controlled_buffer_20
  not not_5 (not_5_out, Outp[4]);
  not not_6 (not_6_out, Outp[5]);
  not not_7 (not_7_out, Outp[6]);
  not not_8 (not_8_out, Outp[7]);
  and and_3 (and_3_out, not_8_out, not_7_out, not_6_out, Outp[4]);
  and and_4 (and_4_out, not_8_out, not_7_out, Outp[5], not_5_out);
  and and_5 (and_5_out, not_8_out, not_7_out, Outp[5], Outp[4]);
  and and_6 (and_6_out, not_8_out, Outp[6], not_6_out, not_5_out);
  and and_7 (and_7_out, not_8_out, Outp[6], not_6_out, Outp[4]);
  and and_8 (and_8_out, not_8_out, Outp[6], Outp[5], not_5_out);
  and and_9 (and_9_out, not_8_out, Outp[6], Outp[5], Outp[4]);
  and and_10 (and_10_out, Outp[7], not_7_out, not_6_out, not_5_out);
  and and_11 (and_11_out, Outp[7], not_7_out, not_6_out, Outp[4]);
  and and_12 (and_12_out, Outp[7], not_7_out, Outp[5], not_5_out);
  and and_13 (and_13_out, Outp[7], not_7_out, Outp[5], Outp[4]);
  and and_14 (and_14_out, Outp[7], Outp[6], not_6_out, not_5_out);
  and and_15 (and_15_out, Outp[7], Outp[6], not_6_out, Outp[4]);
  and and_16 (and_16_out, Outp[7], Outp[6], Outp[5], not_5_out);
  and and_17 (and_17_out, Outp[7], Outp[6], Outp[5], Outp[4]);
  and and_18 (and_18_out, not_8_out, not_7_out, not_6_out, not_5_out);
  or or_6 (or_6_out, and_3_out, and_5_out, and_6_out, and_7_out, and_8_out, and_9_out, and_10_out, and_11_out, and_12_out, and_13_out, and_15_out, and_18_out);
  or or_7 (or_7_out, and_4_out, and_7_out, and_8_out, and_10_out, and_11_out, and_13_out, and_14_out, and_15_out, and_16_out, and_5_out, and_18_out);
  or or_8 (or_8_out, and_4_out, and_8_out, and_10_out, and_12_out, and_13_out, and_14_out, and_15_out, and_16_out, and_17_out, and_18_out);
  or or_9 (or_9_out, and_3_out, and_4_out, and_5_out, and_6_out, and_9_out, and_10_out, and_11_out, and_12_out, and_15_out, and_18_out);
  or or_10 (or_10_out, and_4_out, and_5_out, and_7_out, and_8_out, and_9_out, and_10_out, and_11_out, and_12_out, and_14_out, and_16_out, and_17_out, and_18_out);
  or or_11 (or_11_out, and_6_out, and_7_out, and_8_out, and_10_out, and_11_out, and_12_out, and_13_out, and_14_out, and_16_out, and_17_out, and_18_out);
  or or_12 (or_12_out, and_4_out, and_5_out, and_6_out, and_7_out, and_8_out, and_10_out, and_11_out, and_12_out, and_13_out, and_15_out, and_16_out, and_17_out);
  _7_Segment_Display u_7_segment_display_1 (
    .g(or_12_out), .f(or_11_out), .a(or_10_out), .b(or_9_out), .e(or_8_out), .d(or_7_out), .c(or_6_out));  // open: dp
  _7_Segment_Display u_7_segment_display_2 (
    .g(or_19_out), .f(or_18_out), .a(or_17_out), .b(or_16_out), .e(or_15_out), .d(or_14_out), .c(or_13_out));  // open: dp
  not not_9 (not_9_out, Outp[0]);
  not not_10 (not_10_out, Outp[1]);
  not not_11 (not_11_out, Outp[2]);
  not not_12 (not_12_out, Outp[3]);
  and and_19 (and_19_out, not_12_out, not_11_out, not_10_out, Outp[0]);
  and and_20 (and_20_out, not_12_out, not_11_out, Outp[1], not_9_out);
  and and_21 (and_21_out, not_12_out, not_11_out, Outp[1], Outp[0]);
  and and_22 (and_22_out, not_12_out, Outp[2], not_10_out, not_9_out);
  and and_23 (and_23_out, not_12_out, Outp[2], not_10_out, Outp[0]);
  and and_24 (and_24_out, not_12_out, Outp[2], Outp[1], not_9_out);
  and and_25 (and_25_out, not_12_out, Outp[2], Outp[1], Outp[0]);
  and and_26 (and_26_out, Outp[3], not_11_out, not_10_out, not_9_out);
  and and_27 (and_27_out, Outp[3], not_11_out, not_10_out, Outp[0]);
  and and_28 (and_28_out, Outp[3], not_11_out, Outp[1], not_9_out);
  and and_29 (and_29_out, Outp[3], not_11_out, Outp[1], Outp[0]);
  and and_30 (and_30_out, Outp[3], Outp[2], not_10_out, not_9_out);
  and and_31 (and_31_out, Outp[3], Outp[2], not_10_out, Outp[0]);
  and and_32 (and_32_out, Outp[3], Outp[2], Outp[1], not_9_out);
  and and_33 (and_33_out, Outp[3], Outp[2], Outp[1], Outp[0]);
  and and_34 (and_34_out, not_12_out, not_11_out, not_10_out, not_9_out);
  or or_13 (or_13_out, and_19_out, and_21_out, and_22_out, and_23_out, and_24_out, and_25_out, and_26_out, and_27_out, and_28_out, and_29_out, and_31_out, and_34_out);
  or or_14 (or_14_out, and_20_out, and_23_out, and_24_out, and_26_out, and_27_out, and_29_out, and_30_out, and_31_out, and_32_out, and_21_out, and_34_out);
  or or_15 (or_15_out, and_20_out, and_24_out, and_26_out, and_28_out, and_29_out, and_30_out, and_31_out, and_32_out, and_33_out, and_34_out);
  or or_16 (or_16_out, and_19_out, and_20_out, and_21_out, and_22_out, and_25_out, and_26_out, and_27_out, and_28_out, and_31_out, and_34_out);
  or or_17 (or_17_out, and_20_out, and_21_out, and_23_out, and_24_out, and_25_out, and_26_out, and_27_out, and_28_out, and_30_out, and_32_out, and_33_out, and_34_out);
  or or_18 (or_18_out, and_22_out, and_23_out, and_24_out, and_26_out, and_27_out, and_28_out, and_29_out, and_30_out, and_32_out, and_33_out, and_34_out);
  or or_19 (or_19_out, and_20_out, and_21_out, and_22_out, and_23_out, and_24_out, and_26_out, and_27_out, and_28_out, and_29_out, and_31_out, and_32_out, and_33_out);
endmodule
